// Logisim project CRC.circ as structural Verilog: 3 circuits, main circuit CRC
module CRC (
  input  [7:0] inputA,
  input  [3:0] inputB,
  output [10:0] out_3
);

  wire _4, _5, _6, _7, _8;
  wire [3:0] divider_1_finalquotient, divider_2_finalquotient, divider_3_finalquotient,
       divider_4_finalquotient, divider_5_finalquotient, temp, temp1;
  wire [3:3] divider_6_finalquotient;
  wire [10:5] dataprocessing_1_out_2;

  // Probe on {dataprocessing_1_out_2, _4, _5, _6, _7, _8}
  dataProcessing dataprocessing_1 (.in_1(inputA), .out_2({dataprocessing_1_out_2, _4, _5, _6, _7, _8}));
  divider divider_1 (
    .divided(dataprocessing_1_out_2[10:7]), .dividing(inputB), .finalQuotient(divider_1_finalquotient));
  divider divider_2 (.divided({temp[2:0], _4}), .dividing(inputB), .finalQuotient(divider_2_finalquotient));
  divider divider_3 (.divided({temp1[2:0], _7}), .dividing(inputB), .finalQuotient(divider_3_finalquotient));
  divider divider_4 (
    .divided({divider_1_finalquotient[2:0], dataprocessing_1_out_2[6]}), .dividing(inputB),
    .finalQuotient(divider_4_finalquotient));
  divider divider_5 (
    .divided({divider_2_finalquotient[2:0], _5}), .dividing(inputB), .finalQuotient(divider_5_finalquotient));
  divider divider_6 (
    .divided({divider_3_finalquotient[2:0], _8}), .dividing(inputB),
    .finalQuotient({divider_6_finalquotient[3], out_3[2:0]}));
  divider divider_7 (
    .divided({divider_4_finalquotient[2:0], dataprocessing_1_out_2[5]}), .dividing(inputB),
    .finalQuotient(temp));
  divider divider_8 (.divided({divider_5_finalquotient[2:0], _6}), .dividing(inputB), .finalQuotient(temp1));

  assign out_3[10:3] = inputA;

  // Other names for the same wires on the sheet: dividing[3:0] = inputB; check[2:0] = out_3[2:0];
  //   output[10:0] = {inputA, out_3[2:0]}
endmodule

module divider (
  input  [3:0] divided,
  input  [3:0] dividing,
  output [3:0] finalQuotient
);

  wire [3:0] quotient;

  Multiplexer #(.width(4)) multiplexer_1 (
    .in0(divided), .in1(quotient), .out(finalQuotient), .sel(divided[3]));  // open: en
  assign quotient = divided ^ dividing;  // XOR_Gate xor_1, 4 bits wide

  // Other names for the same wires on the sheet: result = divided[3]
endmodule

module dataProcessing (
  input  [7:0] in_1,
  output [10:0] out_2
);

  assign {out_2[0], out_2[1], out_2[2], out_2[3], out_2[4], out_2[5], out_2[6], out_2[7], out_2[8], out_2[9], out_2[10]} = {{3{1'b0}}, {in_1[0], in_1[1], in_1[2], in_1[3], in_1[4], in_1[5], in_1[6], in_1[7]}};  // Bit_Extender bit_extender_1
endmodule
