// Logisim project Navigate.circ as structural Verilog: 2 circuits, main circuit navigation
module navigation (
  input  clk,
  input  reset,
  input  [1:0] dir,
  output hit,
  output arr
);

  wire [1:0] register_2_q;
  wire [2:0] register_1_q, state_1_s01;

  // Probe on register_1_q
  Register #(.width(3)) register_1 (.D(state_1_s01), .Q(register_1_q), .clk(clk), .clr(reset));  // open: en
  Register #(.width(2)) register_2 (.D(dir), .Q(register_2_q), .clk(clk), .clr(reset));  // open: en
  state state_1 (
    .S2(register_1_q[2]), .S1(register_1_q[1]), .S0(register_1_q[0]), .I1(register_2_q[1]),
    .I0(register_2_q[0]), .s21(state_1_s01[2]), .s11(state_1_s01[1]), .s01(state_1_s01[0]), .hit(hit),
    .arr(arr));
  // Probe on state_1_s01
endmodule

module state (
  input  S2,
  input  S1,
  input  S0,
  input  I1,
  input  I0,
  output s21,
  output s11,
  output s01,
  output hit,
  output arr
);

  wire and_1_out, and_2_out, and_3_out, and_4_out, and_5_out, and_6_out, and_7_out, and_8_out, and_9_out,
       and_10_out, and_11_out, and_12_out, and_13_out, and_14_out, and_15_out, and_16_out, and_17_out,
       and_18_out, not_1_out, not_2_out, not_3_out, not_4_out, not_5_out, not_6_out, not_7_out, not_8_out,
       not_9_out, not_10_out, not_11_out, not_12_out, not_13_out, not_14_out, not_15_out, not_16_out,
       not_17_out, not_18_out, not_19_out, not_20_out, not_21_out, not_22_out, not_23_out, not_24_out,
       not_25_out, not_26_out, not_27_out, not_28_out, not_29_out, not_30_out, not_31_out, not_32_out;

  not not_1 (not_1_out, S0);
  not not_2 (not_2_out, I1);
  not not_3 (not_3_out, I0);
  not not_4 (not_4_out, I1);
  not not_5 (not_5_out, S1);
  not not_6 (not_6_out, I1);
  not not_7 (not_7_out, I1);
  not not_8 (not_8_out, I0);
  not not_9 (not_9_out, S0);
  not not_10 (not_10_out, I1);
  not not_11 (not_11_out, S0);
  not not_12 (not_12_out, I0);
  not not_13 (not_13_out, S2);
  not not_14 (not_14_out, S1);
  not not_15 (not_15_out, I1);
  not not_16 (not_16_out, I0);
  not not_17 (not_17_out, I0);
  not not_18 (not_18_out, S2);
  not not_19 (not_19_out, S0);
  not not_20 (not_20_out, I1);
  not not_21 (not_21_out, S2);
  not not_22 (not_22_out, S1);
  not not_23 (not_23_out, S0);
  not not_24 (not_24_out, S2);
  not not_25 (not_25_out, S0);
  not not_26 (not_26_out, I0);
  not not_27 (not_27_out, I1);
  not not_28 (not_28_out, I0);
  not not_29 (not_29_out, S0);
  not not_30 (not_30_out, I1);
  not not_31 (not_31_out, I0);
  not not_32 (not_32_out, I1);
  and and_1 (and_1_out, S1, not_1_out, not_2_out, not_3_out);
  and and_2 (and_2_out, S1, S0, not_4_out, I0);
  and and_3 (and_3_out, not_5_out, S0, not_6_out);
  and and_4 (and_4_out, S0, not_7_out, not_8_out);
  and and_5 (and_5_out, S1, not_9_out, not_10_out, I0);
  and and_6 (and_6_out, S1, not_11_out, I1, not_12_out);
  and and_7 (and_7_out, S1, S0, I1, I0);
  and and_8 (and_8_out, not_13_out, not_14_out, not_15_out, not_16_out);
  and and_9 (and_9_out, S0, I1, I0);
  and and_10 (and_10_out, S1, I1, I0);
  and and_11 (and_11_out, S1, S0, not_17_out);
  and and_12 (and_12_out, not_18_out, not_19_out, not_20_out, I0);
  and and_13 (and_13_out, not_21_out, not_22_out, not_23_out, I1);
  and and_14 (and_14_out, not_24_out, not_25_out, I1, not_26_out);
  and and_15 (and_15_out, S0, I1, I0);
  and and_16 (and_16_out, S1, S0, not_27_out, not_28_out);
  and and_17 (and_17_out, S1, not_29_out, not_30_out, not_31_out);
  and and_18 (and_18_out, S1, S0, not_32_out, I0);
  or or_1 (s21, and_1_out, and_2_out);
  or or_2 (s11, and_3_out, and_4_out, and_5_out, and_6_out, and_7_out);
  or or_3 (s01, and_8_out, and_9_out, and_10_out, and_11_out);
  or or_4 (hit, and_12_out, and_13_out, and_14_out, and_15_out, and_16_out);
  or or_5 (arr, and_17_out, and_18_out);
endmodule
