// Logisim project Regex Matching.circ as structural Verilog: 3 circuits, main circuit fsm
module fsm (
  input  [1:0] In,
  input  CLR,
  output Z
);

  wire clk_out;
  wire [2:0] multiplexer_1_out, next_state, state_1_s01;

  // Probe on next_state
  state state_1 (
    .S2(next_state[2]), .S1(next_state[1]), .S0(next_state[0]), .I1(In[1]), .I0(In[0]), .S21(state_1_s01[2]),
    .S11(state_1_s01[1]), .S01(state_1_s01[0]));  // open: Z
  Clock clk (.out(clk_out));
  Multiplexer #(.width(3)) multiplexer_1 (
    .in0(state_1_s01), .in1(3'b000), .out(multiplexer_1_out), .sel(CLR));  // open: en
  Register #(.width(3)) register_1 (.D(multiplexer_1_out), .Q(next_state), .clk(clk_out));  // open: en, clr
  \output  output_1 (.S21(next_state[2]), .S11(next_state[1]), .S01(next_state[0]), .I1(In[1]), .I0(In[0]), .out(Z));
endmodule

// FSM
module state (
  input  S2,
  input  S1,
  input  S0,
  input  I1,
  input  I0,
  output S21,
  output S11,
  output S01,
  output Z
);

  wire and_2_out, and_3_out, and_4_out, and_5_out, and_6_out, and_7_out, not_1_out, not_2_out, not_3_out,
       not_4_out, not_5_out, not_6_out, not_7_out, not_8_out, not_9_out, not_10_out, not_11_out, not_12_out,
       not_13_out, not_14_out;

  not not_1 (not_1_out, I0);
  not not_2 (not_2_out, S1);
  not not_3 (not_3_out, I1);
  not not_4 (not_4_out, S1);
  not not_5 (not_5_out, I0);
  not not_6 (not_6_out, S0);
  not not_7 (not_7_out, I0);
  not not_8 (not_8_out, S0);
  not not_9 (not_9_out, I1);
  not not_10 (not_10_out, S1);
  not not_11 (not_11_out, I0);
  not not_12 (not_12_out, S0);
  not not_13 (not_13_out, I0);
  not not_14 (not_14_out, I0);
  and and_1 (S21, S1, S0, not_1_out);
  and and_2 (and_2_out, not_2_out, S0, not_3_out);
  and and_3 (and_3_out, not_4_out, S0, not_5_out);
  and and_4 (and_4_out, S1, not_6_out, not_7_out);
  and and_5 (and_5_out, not_8_out, not_9_out, I0);
  and and_6 (and_6_out, not_10_out, S0, not_11_out);
  and and_7 (and_7_out, S1, not_12_out, not_13_out);
  and and_8 (Z, S1, S0, not_14_out);
  or or_1 (S11, and_2_out, and_3_out, and_4_out);
  or or_2 (S01, and_5_out, and_6_out, and_7_out);
endmodule

module \output  (
  input  S21,
  input  S11,
  input  S01,
  input  I1,
  input  I0,
  output out
);

  wire not_1_out;

  not not_1 (not_1_out, I0);
  and and_1 (out, S11, S01, not_1_out);
endmodule
