// Logisim project CPU.circ as structural Verilog: 9 circuits, main circuit main
module main (
  input  Reset,
  output [31:0] Instr32,
  output [31:0] PC32,
  output RegWrite1,
  output [4:0] RA5,
  output [31:0] RD32,
  output WriteData1,
  output [31:0] MemA32,
  output [31:0] MemD32
);

  wire alu_1_zero, ALUsrc, and_1_out, Clk, ExtRes, MemToReg, PCsrc, ReadData, RegDst, ShfToReg;
  wire [1:0] ALUop;
  wire [11:0] pc_1_instr_addr;
  wire [31:0] adder_1_out, adder_2_out, bit_extender_1_out, bit_extender_2_out, dm_1_readdata_2,
       grf_1_read_data_1, multiplexer_2_out, multiplexer_3_out, multiplexer_5_out, multiplexer_6_out,
       shifter_1_out, shifter_2_out;

  Clock clock_1 (.out(Clk));
  PC pc_1 (.PC_prime(multiplexer_5_out), .PC(PC32), .Instr_Addr(pc_1_instr_addr), .Clk(Clk), .Reset(Reset));
  // Probe on pc_1_instr_addr
  Ctrl_Unit ctrl_unit_1 (
    .Op(Instr32[31:26]), .Func(Instr32[5:0]), .DM_ReadData(ReadData), .DM_WriteData(WriteData1),
    .MemToReg(MemToReg), .PCsrc(PCsrc), .ALUop(ALUop), .RegDst(RegDst), .ALUsrc(ALUsrc), .ShfToReg(ShfToReg),
    .RegWrite(RegWrite1), .ExtRes(ExtRes));
  // Mips_Probe mips_probe_1: pin names not known; wires that end beside it: Instr32
  IM im_1 (.Read_Addr(pc_1_instr_addr), .Instruction(Instr32));
  Adder #(.width(32)) adder_1 (.a(32'h4), .b(PC32), .out(adder_1_out));  // open: cin, cout
  // Probe on Instr32
  // Probe on Instr32[31:26]
  // Probe on Instr32[25:21]
  Multiplexer #(.width(5), .enable("false")) multiplexer_1 (
    .in0(Instr32[20:16]), .in1(Instr32[15:11]), .out(RA5), .sel(RegDst));
  // Probe on Instr32[15:0]
  assign bit_extender_1_out = {{16{Instr32[15]}}, Instr32[15:0]};  // Bit_Extender bit_extender_1
  assign bit_extender_2_out = {{16{1'b0}}, Instr32[15:0]};  // Bit_Extender bit_extender_2
  GRF grf_1 (
    .Clk(Clk), .Reset(Reset), .WD(RD32), .A3(RA5), .A2(Instr32[20:16]), .Read_Data_2(MemD32),
    .Read_Data_1(grf_1_read_data_1), .A1(Instr32[25:21]), .RegWrite(RegWrite1));
  Multiplexer #(.width(32), .enable("false")) multiplexer_2 (
    .in0(bit_extender_1_out), .in1(bit_extender_2_out), .out(multiplexer_2_out), .sel(ExtRes));
  Shifter #(.width(32)) shifter_1 (.in(multiplexer_2_out), .\dist (5'b00010), .out(shifter_1_out));
  Multiplexer #(.width(32), .enable("false")) multiplexer_3 (
    .in0(MemD32), .in1(multiplexer_2_out), .out(multiplexer_3_out), .sel(ALUsrc));
  Multiplexer #(.width(32), .enable("false")) multiplexer_4 (
    .in0(multiplexer_6_out), .in1(shifter_2_out), .out(RD32), .sel(ShfToReg));
  Shifter #(.width(32)) shifter_2 (.in(multiplexer_2_out), .\dist (5'b10000), .out(shifter_2_out));
  // Probe on Instr32
  // Probe on PC32
  // Probe on RD32
  // Probe on MemA32
  // Probe on MemD32
  Adder #(.width(32)) adder_2 (.a(adder_1_out), .b(shifter_1_out), .out(adder_2_out));  // open: cin, cout
  and and_1 (and_1_out, alu_1_zero, PCsrc);
  ALU alu_1 (.srcA(grf_1_read_data_1), .srcB(multiplexer_3_out), .ALUop(ALUop), .Result(MemA32), .Zero(alu_1_zero));
  Multiplexer #(.width(32), .enable("false")) multiplexer_5 (
    .in0(adder_1_out), .in1(adder_2_out), .out(multiplexer_5_out), .sel(and_1_out));
  // Probe on MemA32
  // Probe on multiplexer_6_out
  DM dm_1 (
    .Clk(Clk), .ReadData(ReadData), .ReadData_2(dm_1_readdata_2), .Reset(Reset), .WriteData_2(WriteData1),
    .WriteData(MemD32), .Addr(MemA32));
  Multiplexer #(.width(32), .enable("false")) multiplexer_6 (
    .in0(dm_1_readdata_2), .in1(MemA32), .out(multiplexer_6_out), .sel(MemToReg));

  // Other names for the same wires on the sheet: Instr[31:0] = Instr32; Func[5:0] = Instr32[5:0];
  //   Op[5:0] = Instr32[31:26]; MemA[31:0] = MemA32; MemD[31:0] = MemD32; PC[31:0] = PC32; RA[4:0] = RA5;
  //   RD[31:0] = RD32; RegWrite = RegWrite1; WriteData = WriteData1
endmodule

module PC (
  input  Clk,
  input  Reset,
  input  [31:0] PC_prime,
  output [11:0] Instr_Addr,
  output [31:0] PC
);

  wire comparator_1_eq;
  wire [31:0] PC_Reg_q, subtractor_1_out;

  // Probe on PC_prime
  Register #(.width(32)) PC_Reg (.D(PC_prime), .Q(PC_Reg_q), .clk(Clk), .clr(Reset));  // open: en
  Comparator #(.width(32), .mode("unsigned")) comparator_1 (
    .a(PC_Reg_q), .b({32{1'b0}}), .eq(comparator_1_eq));  // open: gt, lt
  Multiplexer #(.width(32), .enable("false")) multiplexer_1 (
    .in0(PC_Reg_q), .in1(32'h3000), .out(PC), .sel(comparator_1_eq));
  Subtractor #(.width(32)) subtractor_1 (
    .a(PC), .b(32'h3000), .out({subtractor_1_out[31:14], Instr_Addr, subtractor_1_out[1:0]}));  // open: bin, bout
  // Probe on Instr_Addr
endmodule

module IM (
  input  [11:0] Read_Addr,
  output [31:0] Instruction
);

  ROM #(.addrWidth(12), .dataWidth(32)) rom_1 (.addr(Read_Addr), .data(Instruction));  // open: sel

  // Notes on the sheet:
  //   contents of rom_1 (hex, n*v repeats v):
  //   3404007b 348501c8 3c06007b 3c07ffff 34e7ffff 868020 878820 e79020 34080000 ad040000 ad050004
  //   ad060008 ad07000c ad100010 ad110014 ad120018 8d040000 8d05000c ad04001c ad050020 34040001 34050002
  //   34060001 10850001 10860001 ad040024 ad050028
endmodule

module GRF (
  input  Clk,
  input  Reset,
  input  RegWrite,
  input  [31:0] WD,
  input  [4:0] A3,
  input  [4:0] A2,
  input  [4:0] A1,
  output [31:0] Read_Data_2,
  output [31:0] Read_Data_1
);

  wire [31:0] In0, In1, In2, In3, In4, In5, In6, In7, In8, In9, In10, In11, In12, In13, In14, In15, In16,
       In17, In18, In19, In20, In21, In22, In23, In24, In25, In26, In27, In28, In29, In30, In31, Out0, Out1,
       Out2, Out3, Out4, Out5, Out6, Out7, Out8, Out9, Out10, Out11, Out12, Out13, Out14, Out15, Out16,
       Out17, Out18, Out19, Out20, Out21, Out22, Out23, Out24, Out25, Out26, Out27, Out28, Out29, Out30,
       Out31;

  Demultiplexer #(.select(5), .width(32), .tristate("true"), .enable("false")) demultiplexer_1 (
    .out0(In0), .out1(In1), .out2(In2), .out3(In3), .out4(In4), .out5(In5), .out6(In6), .out7(In7),
    .out8(In8), .out9(In9), .out10(In10), .out11(In11), .out12(In12), .out13(In13), .out14(In14),
    .out15(In15), .out16(In16), .out17(In17), .out18(In18), .out19(In19), .out20(In20), .out21(In21),
    .out22(In22), .out23(In23), .out24(In24), .out25(In25), .out26(In26), .out27(In27), .out28(In28),
    .out29(In29), .out30(In30), .out31(In31), .in(WD), .sel(A3));
  Register #(.width(32)) _0 (.D(In0), .en(1'b0), .Q(Out0), .clk(Clk), .clr(Reset));
  Register #(.width(32)) _1 (.D(In1), .en(RegWrite), .Q(Out1), .clk(Clk), .clr(Reset));
  Register #(.width(32)) _2 (.D(In2), .en(RegWrite), .Q(Out2), .clk(Clk), .clr(Reset));
  Register #(.width(32)) _3 (.D(In3), .en(RegWrite), .Q(Out3), .clk(Clk), .clr(Reset));
  Register #(.width(32)) _4 (.D(In4), .en(RegWrite), .Q(Out4), .clk(Clk), .clr(Reset));
  Register #(.width(32)) _5 (.D(In5), .en(RegWrite), .Q(Out5), .clk(Clk), .clr(Reset));
  Register #(.width(32)) _6 (.D(In6), .en(RegWrite), .Q(Out6), .clk(Clk), .clr(Reset));
  Register #(.width(32)) _7 (.D(In7), .en(RegWrite), .Q(Out7), .clk(Clk), .clr(Reset));
  Register #(.width(32)) _8 (.D(In8), .en(RegWrite), .Q(Out8), .clk(Clk), .clr(Reset));
  Register #(.width(32)) _9 (.D(In9), .en(RegWrite), .Q(Out9), .clk(Clk), .clr(Reset));
  Register #(.width(32)) _10 (.D(In10), .en(RegWrite), .Q(Out10), .clk(Clk), .clr(Reset));
  Register #(.width(32)) _11 (.D(In11), .en(RegWrite), .Q(Out11), .clk(Clk), .clr(Reset));
  Register #(.width(32)) _12 (.D(In12), .en(RegWrite), .Q(Out12), .clk(Clk), .clr(Reset));
  Register #(.width(32)) _13 (.D(In13), .en(RegWrite), .Q(Out13), .clk(Clk), .clr(Reset));
  Register #(.width(32)) _14 (.D(In14), .en(RegWrite), .Q(Out14), .clk(Clk), .clr(Reset));
  Register #(.width(32)) _15 (.D(In15), .en(RegWrite), .Q(Out15), .clk(Clk), .clr(Reset));
  Multiplexer #(.select(5), .width(32), .enable("false")) multiplexer_1 (
    .in0(Out0), .in1(Out1), .in2(Out2), .in3(Out3), .in4(Out4), .in5(Out5), .in6(Out6), .in7(Out7),
    .in8(Out8), .in9(Out9), .in10(Out10), .in11(Out11), .in12(Out12), .in13(Out13), .in14(Out14),
    .in15(Out15), .in16(Out16), .in17(Out17), .in18(Out18), .in19(Out19), .in20(Out20), .in21(Out21),
    .in22(Out22), .in23(Out23), .in24(Out24), .in25(Out25), .in26(Out26), .in27(Out27), .in28(Out28),
    .in29(Out29), .in30(Out30), .in31(Out31), .out(Read_Data_2), .sel(A2));
  Register #(.width(32)) _16 (.D(In16), .en(RegWrite), .Q(Out16), .clk(Clk), .clr(Reset));
  Register #(.width(32)) _17 (.D(In17), .en(RegWrite), .Q(Out17), .clk(Clk), .clr(Reset));
  Register #(.width(32)) _18 (.D(In18), .en(RegWrite), .Q(Out18), .clk(Clk), .clr(Reset));
  Register #(.width(32)) _19 (.D(In19), .en(RegWrite), .Q(Out19), .clk(Clk), .clr(Reset));
  Register #(.width(32)) _20 (.D(In20), .en(RegWrite), .Q(Out20), .clk(Clk), .clr(Reset));
  Register #(.width(32)) _21 (.D(In21), .en(RegWrite), .Q(Out21), .clk(Clk), .clr(Reset));
  Register #(.width(32)) _22 (.D(In22), .en(RegWrite), .Q(Out22), .clk(Clk), .clr(Reset));
  Register #(.width(32)) _23 (.D(In23), .en(RegWrite), .Q(Out23), .clk(Clk), .clr(Reset));
  Register #(.width(32)) _24 (.D(In24), .en(RegWrite), .Q(Out24), .clk(Clk), .clr(Reset));
  Register #(.width(32)) _25 (.D(In25), .en(RegWrite), .Q(Out25), .clk(Clk), .clr(Reset));
  Register #(.width(32)) _26 (.D(In26), .en(RegWrite), .Q(Out26), .clk(Clk), .clr(Reset));
  Register #(.width(32)) _27 (.D(In27), .en(RegWrite), .Q(Out27), .clk(Clk), .clr(Reset));
  Multiplexer #(.select(5), .width(32), .enable("false")) multiplexer_2 (
    .in0(Out0), .in1(Out1), .in2(Out2), .in3(Out3), .in4(Out4), .in5(Out5), .in6(Out6), .in7(Out7),
    .in8(Out8), .in9(Out9), .in10(Out10), .in11(Out11), .in12(Out12), .in13(Out13), .in14(Out14),
    .in15(Out15), .in16(Out16), .in17(Out17), .in18(Out18), .in19(Out19), .in20(Out20), .in21(Out21),
    .in22(Out22), .in23(Out23), .in24(Out24), .in25(Out25), .in26(Out26), .in27(Out27), .in28(Out28),
    .in29(Out29), .in30(Out30), .in31(Out31), .out(Read_Data_1), .sel(A1));
  Register #(.width(32)) _28 (.D(In28), .en(RegWrite), .Q(Out28), .clk(Clk), .clr(Reset));
  Register #(.width(32)) _29 (.D(In29), .en(RegWrite), .Q(Out29), .clk(Clk), .clr(Reset));
  Register #(.width(32)) _30 (.D(In30), .en(RegWrite), .Q(Out30), .clk(Clk), .clr(Reset));
  Register #(.width(32)) _31 (.D(In31), .en(RegWrite), .Q(Out31), .clk(Clk), .clr(Reset));

  // Other names for the same wires on the sheet: En = RegWrite
endmodule

module Ctrl_1 (
  input  [5:0] Op,
  input  [5:0] Func,
  output ADD,
  output ORI,
  output SUB,
  output LW,
  output SW,
  output BEQ,
  output LUI
);

  wire R_out;

  and R (R_out, ~Op[5], ~Op[4], ~Op[3], ~Op[2], ~Op[1], ~Op[0]);  // AND_Gate
  and u_ORI (ORI, ~Op[5], ~Op[4], Op[3], Op[2], ~Op[1], Op[0]);  // AND_Gate
  and u_LW (LW, Op[5], ~Op[4], ~Op[3], ~Op[2], Op[1], Op[0]);  // AND_Gate
  and u_SW (SW, Op[5], ~Op[4], Op[3], ~Op[2], Op[1], Op[0]);  // AND_Gate
  and u_BEQ (BEQ, ~Op[5], ~Op[4], ~Op[3], Op[2], ~Op[1], ~Op[0]);  // AND_Gate
  and u_LUI (LUI, ~Op[5], ~Op[4], Op[3], Op[2], Op[1], Op[0]);  // AND_Gate
  and u_ADD (ADD, R_out, Func[5], ~Func[4], ~Func[3], ~Func[2], ~Func[1], ~Func[0]);  // AND_Gate
  and u_SUB (SUB, R_out, Func[5], ~Func[4], ~Func[3], ~Func[2], Func[1], ~Func[0]);  // AND_Gate

  // Notes on the sheet:
  //   Op[5:0]
endmodule

module Ctrl_Unit (
  input  [5:0] Op,
  input  [5:0] Func,
  output DM_ReadData,
  output DM_WriteData,
  output MemToReg,
  output PCsrc,
  output RegDst,
  output ALUsrc,
  output ShfToReg,
  output RegWrite,
  output [1:0] ALUop,
  output ExtRes
);

  wire ctrl_1_1_add, ctrl_1_1_beq, ctrl_1_1_lui, ctrl_1_1_lw, ctrl_1_1_ori, ctrl_1_1_sub, ctrl_1_1_sw;

  Ctrl_1 ctrl_1_1 (
    .Op(Op), .Func(Func), .ADD(ctrl_1_1_add), .SUB(ctrl_1_1_sub), .ORI(ctrl_1_1_ori), .LW(ctrl_1_1_lw),
    .SW(ctrl_1_1_sw), .BEQ(ctrl_1_1_beq), .LUI(ctrl_1_1_lui));
  buf or_1 (DM_ReadData, ctrl_1_1_lw);  // OR_Gate
  buf or_2 (DM_WriteData, ctrl_1_1_sw);  // OR_Gate
  or or_3 (MemToReg, ctrl_1_1_add, ctrl_1_1_sub, ctrl_1_1_ori);
  buf or_4 (PCsrc, ctrl_1_1_beq);  // OR_Gate
  or or_5 (RegDst, ctrl_1_1_add, ctrl_1_1_sub);
  or or_6 (ALUsrc, ctrl_1_1_ori, ctrl_1_1_lw, ctrl_1_1_sw);
  buf or_7 (ShfToReg, ctrl_1_1_lui);  // OR_Gate
  or or_8 (RegWrite, ctrl_1_1_add, ctrl_1_1_sub, ctrl_1_1_ori, ctrl_1_1_lw, ctrl_1_1_lui);
  Signal signal_1 (
    .ADD(ctrl_1_1_add), .SUB(ctrl_1_1_sub), .ORI(ctrl_1_1_ori), .LW(ctrl_1_1_lw), .SW(ctrl_1_1_sw),
    .BEQ(ctrl_1_1_beq), .LUI(ctrl_1_1_lui), .ALUop1(ALUop[1]), .ALUop0(ALUop[0]));
  buf or_9 (ExtRes, ctrl_1_1_ori);  // OR_Gate
endmodule

module ALU (
  input  [31:0] srcA,
  input  [1:0] ALUop,
  input  [31:0] srcB,
  output Zero,
  output [31:0] Result
);

  wire [31:0] Add, And, Or, Sub;

  Adder #(.width(32)) adder_1 (.a(srcA), .b(srcB), .out(Add));  // open: cin, cout
  Subtractor #(.width(32)) subtractor_1 (.a(srcA), .b(srcB), .out(Sub));  // open: bin, bout
  assign And = srcA & srcB;  // AND_Gate and_1, 32 bits wide
  assign Or = srcA | srcB;  // OR_Gate or_1, 32 bits wide
  Multiplexer #(.select(2), .width(32), .enable("false")) multiplexer_1 (
    .in0(Add), .in1(Sub), .in2(And), .in3(Or), .out(Result), .sel(ALUop));
  Comparator #(.width(32), .mode("unsigned")) comparator_1 (.a(Result), .b({32{1'b0}}), .eq(Zero));  // open: gt, lt

  // Notes on the sheet:
  //   00：Add；01：Sub；10：And；11：Or
  //   Unsigned Comparator
endmodule

module DM (
  input  [31:0] Addr,
  input  [31:0] WriteData,
  input  Reset,
  input  WriteData_2,
  input  Clk,
  input  ReadData,
  output [31:0] ReadData_2
);

  RAM #(.addrWidth(12), .dataWidth(32), .bus("separate")) ram_1 (
    .addr(Addr[13:2]), .din(WriteData), .data(ReadData_2), .str(WriteData_2), .clk(Clk), .ld(ReadData),
    .clr(Reset));  // open: sel
endmodule

module Signal (
  input  ADD,
  input  SUB,
  input  ORI,
  input  LW,
  input  SW,
  input  BEQ,
  input  LUI,
  output ALUop1,
  output ALUop0
);

  wire and_1_out, and_2_out, and_3_out, and_4_out, and_5_out, and_6_out, and_7_out, and_8_out, and_9_out,
       and_10_out, and_11_out, and_12_out, not_1_out, not_2_out, not_3_out, not_4_out, not_5_out, not_6_out,
       not_7_out, not_8_out, not_9_out, not_10_out, not_11_out, not_12_out, not_13_out, not_14_out,
       not_15_out, not_16_out, not_17_out, not_18_out, not_19_out, not_20_out, not_21_out;

  not not_1 (not_1_out, SUB);
  not not_2 (not_2_out, LW);
  not not_3 (not_3_out, SW);
  not not_4 (not_4_out, SUB);
  not not_5 (not_5_out, LW);
  not not_6 (not_6_out, BEQ);
  not not_7 (not_7_out, LUI);
  not not_8 (not_8_out, LW);
  not not_9 (not_9_out, SW);
  not not_10 (not_10_out, LUI);
  not not_11 (not_11_out, ADD);
  not not_12 (not_12_out, SUB);
  not not_13 (not_13_out, LW);
  not not_14 (not_14_out, BEQ);
  not not_15 (not_15_out, LUI);
  not not_16 (not_16_out, LW);
  not not_17 (not_17_out, SW);
  not not_18 (not_18_out, LUI);
  not not_19 (not_19_out, LW);
  not not_20 (not_20_out, SW);
  not not_21 (not_21_out, LUI);
  and and_1 (and_1_out, not_1_out, not_2_out, not_3_out, BEQ, LUI);
  and and_2 (and_2_out, not_4_out, ORI, not_5_out, not_6_out, not_7_out);
  and and_3 (and_3_out, ADD, LUI);
  and and_4 (and_4_out, ADD, BEQ);
  and and_5 (and_5_out, ADD, SW);
  and and_6 (and_6_out, ADD, LW);
  and and_7 (and_7_out, ADD, ORI);
  and and_8 (and_8_out, ADD, SUB);
  and and_9 (and_9_out, not_8_out, not_9_out, BEQ, not_10_out);
  and and_10 (and_10_out, not_11_out, not_12_out, ORI, not_13_out, not_14_out, not_15_out);
  and and_11 (and_11_out, ORI, not_16_out, not_17_out, not_18_out);
  and and_12 (and_12_out, SUB, not_19_out, not_20_out, not_21_out);
  or or_1 (ALUop0, and_9_out, and_10_out, and_11_out, and_12_out);
  or or_2 (ALUop1, and_1_out, and_2_out, and_3_out, and_4_out, and_5_out, and_6_out, and_7_out, and_8_out);
endmodule
