// Logisim project GRF.circ as structural Verilog: 1 circuit, main circuit grf
module grf (
  input  clk,
  input  reset,
  input  WE,
  input  [4:0] A1,
  input  [4:0] A2,
  input  [4:0] A3,
  input  [31:0] WD,
  output [31:0] RD1,
  output [31:0] RD2
);

  wire WE1, WE2, WE3, WE4, WE5, WE6, WE7, WE8, WE9, WE10, WE11, WE12, WE13, WE14, WE15, WE16, WE17, WE18,
       WE19, WE20, WE21, WE22, WE23, WE24, WE25, WE26, WE27, WE28, WE29, WE30, WE31, WE32;
  wire [31:0] in1, in2, in3, in4, in5, in6, in7, in8, in9, in10, in11, in12, in13, in14, in15, in16, in17,
       in18, in19, in20, in21, in22, in23, in24, in25, in26, in27, in28, in29, in30, in31, in32, out1, out2,
       out3, out4, out5, out6, out7, out8, out9, out10, out11, out12, out13, out14, out15, out16, out17,
       out18, out19, out20, out21, out22, out23, out24, out25, out26, out27, out28, out29, out30, out31,
       out32;

  Register #(.width(32)) register_1 (.D({32{1'b0}}), .en(WE1), .Q(out1), .clk(clk), .clr(reset));
  Register #(.width(32)) register_2 (.D(in2), .en(WE2), .Q(out2), .clk(clk), .clr(reset));
  Register #(.width(32)) register_3 (.D(in3), .en(WE3), .Q(out3), .clk(clk), .clr(reset));
  Register #(.width(32)) register_4 (.D(in4), .en(WE4), .Q(out4), .clk(clk), .clr(reset));
  Demultiplexer #(.select(5), .width(32)) demultiplexer_1 (
    .out0(in1), .out1(in2), .out2(in3), .out3(in4), .out4(in5), .out5(in6), .out6(in7), .out7(in8),
    .out8(in9), .out9(in10), .out10(in11), .out11(in12), .out12(in13), .out13(in14), .out14(in15),
    .out15(in16), .out16(in17), .out17(in18), .out18(in19), .out19(in20), .out20(in21), .out21(in22),
    .out22(in23), .out23(in24), .out24(in25), .out25(in26), .out26(in27), .out27(in28), .out28(in29),
    .out29(in30), .out30(in31), .out31(in32), .in(WD), .sel(A3));  // open: en
  Register #(.width(32)) register_5 (.D(in5), .en(WE5), .Q(out5), .clk(clk), .clr(reset));
  Register #(.width(32)) register_6 (.D(in6), .en(WE6), .Q(out6), .clk(clk), .clr(reset));
  Register #(.width(32)) register_7 (.D(in7), .en(WE7), .Q(out7), .clk(clk), .clr(reset));
  Register #(.width(32)) register_8 (.D(in8), .en(WE8), .Q(out8), .clk(clk), .clr(reset));
  Register #(.width(32)) register_9 (.D(in9), .en(WE9), .Q(out9), .clk(clk), .clr(reset));
  Register #(.width(32)) register_10 (.D(in10), .en(WE10), .Q(out10), .clk(clk), .clr(reset));
  Register #(.width(32)) register_11 (.D(in11), .en(WE11), .Q(out11), .clk(clk), .clr(reset));
  Register #(.width(32)) register_12 (.D(in12), .en(WE12), .Q(out12), .clk(clk), .clr(reset));
  Demultiplexer #(.select(5)) demultiplexer_2 (
    .out0(WE1), .out1(WE2), .out2(WE3), .out3(WE4), .out4(WE5), .out5(WE6), .out6(WE7), .out7(WE8),
    .out8(WE9), .out9(WE10), .out10(WE11), .out11(WE12), .out12(WE13), .out13(WE14), .out14(WE15),
    .out15(WE16), .out16(WE17), .out17(WE18), .out18(WE19), .out19(WE20), .out20(WE21), .out21(WE22),
    .out22(WE23), .out23(WE24), .out24(WE25), .out25(WE26), .out26(WE27), .out27(WE28), .out28(WE29),
    .out29(WE30), .out30(WE31), .out31(WE32), .in(WE), .sel(A3));  // open: en
  Register #(.width(32)) register_13 (.D(in13), .en(WE13), .Q(out13), .clk(clk), .clr(reset));
  Register #(.width(32)) register_14 (.D(in14), .en(WE14), .Q(out14), .clk(clk), .clr(reset));
  Register #(.width(32)) register_15 (.D(in15), .en(WE15), .Q(out15), .clk(clk), .clr(reset));
  Register #(.width(32)) register_16 (.D(in16), .en(WE16), .Q(out16), .clk(clk), .clr(reset));
  Register #(.width(32)) register_17 (.D(in17), .en(WE17), .Q(out17), .clk(clk), .clr(reset));
  Register #(.width(32)) register_18 (.D(in18), .en(WE18), .Q(out18), .clk(clk), .clr(reset));
  Register #(.width(32)) register_19 (.D(in19), .en(WE19), .Q(out19), .clk(clk), .clr(reset));
  Register #(.width(32)) register_20 (.D(in20), .en(WE20), .Q(out20), .clk(clk), .clr(reset));
  Register #(.width(32)) register_21 (.D(in21), .en(WE21), .Q(out21), .clk(clk), .clr(reset));
  Register #(.width(32)) register_22 (.D(in22), .en(WE22), .Q(out22), .clk(clk), .clr(reset));
  Register #(.width(32)) register_23 (.D(in23), .en(WE23), .Q(out23), .clk(clk), .clr(reset));
  Register #(.width(32)) register_24 (.D(in24), .en(WE24), .Q(out24), .clk(clk), .clr(reset));
  Multiplexer #(.select(5), .width(32)) multiplexer_1 (
    .in0(out1), .in1(out2), .in2(out3), .in3(out4), .in4(out5), .in5(out6), .in6(out7), .in7(out8),
    .in8(out9), .in9(out10), .in10(out11), .in11(out12), .in12(out13), .in13(out14), .in14(out15),
    .in15(out16), .in16(out17), .in17(out18), .in18(out19), .in19(out20), .in20(out21), .in21(out22),
    .in22(out23), .in23(out24), .in24(out25), .in25(out26), .in26(out27), .in27(out28), .in28(out29),
    .in29(out30), .in30(out31), .in31(out32), .out(RD2), .sel(A2));  // open: en
  Multiplexer #(.select(5), .width(32)) multiplexer_2 (
    .in0(out1), .in1(out2), .in2(out3), .in3(out4), .in4(out5), .in5(out6), .in6(out7), .in7(out8),
    .in8(out9), .in9(out10), .in10(out11), .in11(out12), .in12(out13), .in13(out14), .in14(out15),
    .in15(out16), .in16(out17), .in17(out18), .in18(out19), .in19(out20), .in20(out21), .in21(out22),
    .in22(out23), .in23(out24), .in24(out25), .in25(out26), .in26(out27), .in27(out28), .in28(out29),
    .in29(out30), .in30(out31), .in31(out32), .out(RD1), .sel(A1));  // open: en
  Register #(.width(32)) register_25 (.D(in25), .en(WE25), .Q(out25), .clk(clk), .clr(reset));
  Register #(.width(32)) register_26 (.D(in26), .en(WE26), .Q(out26), .clk(clk), .clr(reset));
  Register #(.width(32)) register_27 (.D(in27), .en(WE27), .Q(out27), .clk(clk), .clr(reset));
  Register #(.width(32)) register_28 (.D(in28), .en(WE28), .Q(out28), .clk(clk), .clr(reset));
  Register #(.width(32)) register_29 (.D(in29), .en(WE29), .Q(out29), .clk(clk), .clr(reset));
  Register #(.width(32)) register_30 (.D(in30), .en(WE30), .Q(out30), .clk(clk), .clr(reset));
  Register #(.width(32)) register_31 (.D(in31), .en(WE31), .Q(out31), .clk(clk), .clr(reset));
  Register #(.width(32)) register_32 (.D(in32), .en(WE32), .Q(out32), .clk(clk), .clr(reset));
endmodule
