// Logisim project navigation_new.circ as structural Verilog: 3 circuits, main circuit navigation
module navigation (
  input  [1:0] dir,
  input  clk,
  input  reset,
  output arr,
  output hit
);

  wire [3:0] next_state, register_1_q;

  Register #(.width(4)) register_1 (.D(next_state), .Q(register_1_q), .clk(clk), .clr(reset));  // open: en
  \output  output_1 (
    .S31(register_1_q[3]), .S21(register_1_q[2]), .S11(register_1_q[1]), .S01(register_1_q[0]), .arr(arr),
    .hit(hit));
  state state_1 (
    .S3(register_1_q[3]), .S2(register_1_q[2]), .S1(register_1_q[1]), .S0(register_1_q[0]), .I1(dir[1]),
    .I0(dir[0]), .S31(next_state[3]), .S21(next_state[2]), .S11(next_state[1]), .S01(next_state[0]));
endmodule

module state (
  input  S3,
  input  S2,
  input  S1,
  input  S0,
  input  I1,
  input  I0,
  output S31,
  output S21,
  output S11,
  output S01
);

  wire and_1_out, and_2_out, and_3_out, and_4_out, and_5_out, and_6_out, and_7_out, and_8_out, and_9_out,
       and_10_out, and_11_out, and_12_out, and_13_out, and_14_out, and_15_out, and_16_out, and_17_out,
       and_18_out, and_19_out, and_20_out, and_21_out, and_22_out, and_23_out, and_24_out, and_25_out,
       and_26_out, and_27_out, and_28_out, and_29_out, and_30_out, and_31_out, and_32_out, and_33_out,
       and_34_out, and_35_out, and_36_out, not_1_out, not_2_out, not_3_out, not_4_out, not_5_out, not_6_out,
       not_7_out, not_8_out, not_9_out, not_10_out, not_11_out, not_12_out, not_13_out, not_14_out,
       not_15_out, not_16_out, not_17_out, not_18_out, not_19_out, not_20_out, not_21_out, not_22_out,
       not_23_out, not_24_out, not_25_out, not_26_out, not_27_out, not_28_out, not_29_out, not_30_out,
       not_31_out, not_32_out, not_33_out, not_34_out, not_35_out, not_36_out, not_37_out, not_38_out,
       not_39_out, not_40_out, not_41_out, not_42_out, not_43_out, not_44_out, not_45_out, not_46_out,
       not_47_out, not_48_out, not_49_out, not_50_out, not_51_out, not_52_out, not_53_out, not_54_out,
       not_55_out, not_56_out, not_57_out, not_58_out, not_59_out, not_60_out, not_61_out, not_62_out,
       not_63_out, not_64_out, not_65_out, not_66_out, not_67_out, not_68_out, not_69_out, not_70_out,
       not_71_out, not_72_out, not_73_out, not_74_out, not_75_out, not_76_out, not_77_out, not_78_out,
       not_79_out;

  not not_1 (not_1_out, S2);
  not not_2 (not_2_out, I1);
  not not_3 (not_3_out, I0);
  not not_4 (not_4_out, S2);
  not not_5 (not_5_out, S2);
  not not_6 (not_6_out, S1);
  not not_7 (not_7_out, S0);
  not not_8 (not_8_out, I1);
  not not_9 (not_9_out, I0);
  not not_10 (not_10_out, S2);
  not not_11 (not_11_out, S1);
  not not_12 (not_12_out, S0);
  not not_13 (not_13_out, S2);
  not not_14 (not_14_out, S0);
  not not_15 (not_15_out, I1);
  not not_16 (not_16_out, S3);
  not not_17 (not_17_out, S2);
  not not_18 (not_18_out, S1);
  not not_19 (not_19_out, S0);
  not not_20 (not_20_out, S3);
  not not_21 (not_21_out, S2);
  not not_22 (not_22_out, S1);
  not not_23 (not_23_out, S2);
  not not_24 (not_24_out, S0);
  not not_25 (not_25_out, I0);
  not not_26 (not_26_out, S2);
  not not_27 (not_27_out, I1);
  not not_28 (not_28_out, S3);
  not not_29 (not_29_out, S1);
  not not_30 (not_30_out, S3);
  not not_31 (not_31_out, S1);
  not not_32 (not_32_out, S3);
  not not_33 (not_33_out, S0);
  not not_34 (not_34_out, S3);
  not not_35 (not_35_out, I1);
  not not_36 (not_36_out, S3);
  not not_37 (not_37_out, I0);
  not not_38 (not_38_out, S2);
  not not_39 (not_39_out, S1);
  not not_40 (not_40_out, I1);
  not not_41 (not_41_out, S2);
  not not_42 (not_42_out, S1);
  not not_43 (not_43_out, S0);
  not not_44 (not_44_out, I1);
  not not_45 (not_45_out, S2);
  not not_46 (not_46_out, S0);
  not not_47 (not_47_out, I0);
  not not_48 (not_48_out, S0);
  not not_49 (not_49_out, I1);
  not not_50 (not_50_out, S0);
  not not_51 (not_51_out, I1);
  not not_52 (not_52_out, I0);
  not not_53 (not_53_out, S3);
  not not_54 (not_54_out, S2);
  not not_55 (not_55_out, S1);
  not not_56 (not_56_out, S0);
  not not_57 (not_57_out, S3);
  not not_58 (not_58_out, S2);
  not not_59 (not_59_out, S0);
  not not_60 (not_60_out, S2);
  not not_61 (not_61_out, S0);
  not not_62 (not_62_out, I0);
  not not_63 (not_63_out, S2);
  not not_64 (not_64_out, S1);
  not not_65 (not_65_out, I1);
  not not_66 (not_66_out, I0);
  not not_67 (not_67_out, S2);
  not not_68 (not_68_out, S0);
  not not_69 (not_69_out, I1);
  not not_70 (not_70_out, S2);
  not not_71 (not_71_out, I0);
  not not_72 (not_72_out, S3);
  not not_73 (not_73_out, S1);
  not not_74 (not_74_out, S3);
  not not_75 (not_75_out, S3);
  not not_76 (not_76_out, S0);
  not not_77 (not_77_out, I1);
  not not_78 (not_78_out, I0);
  not not_79 (not_79_out, S0);
  and and_1 (and_1_out, not_1_out, S1, S0, not_2_out, not_3_out);
  and and_2 (and_2_out, not_4_out, S1, S0, I1, I0);
  and and_3 (and_3_out, S3, not_5_out, not_6_out, not_7_out, not_8_out, not_9_out);
  and and_4 (and_4_out, S3, not_10_out, not_11_out, not_12_out, I1, I0);
  and and_5 (and_5_out, not_13_out, not_14_out, not_15_out, I0);
  and and_6 (and_6_out, not_16_out, not_17_out, not_18_out, not_19_out, I1);
  and and_7 (and_7_out, not_20_out, not_21_out, not_22_out, I1, I0);
  and and_8 (and_8_out, not_23_out, S1, not_24_out, not_25_out);
  and and_9 (and_9_out, not_26_out, S1, not_27_out, I0);
  and and_10 (and_10_out, not_28_out, S2, not_29_out, S0, I0);
  and and_11 (and_11_out, not_30_out, S2, not_31_out, S0, I1);
  and and_12 (and_12_out, not_32_out, S2, S1, not_33_out, I1, I0);
  and and_13 (and_13_out, not_34_out, S2, S1, S0, not_35_out);
  and and_14 (and_14_out, not_36_out, S2, S1, S0, not_37_out);
  and and_15 (and_15_out, not_38_out, not_39_out, S0, not_40_out);
  and and_16 (and_16_out, not_41_out, not_42_out, S0, I0);
  and and_17 (and_17_out, S1, not_43_out, not_44_out, I0);
  and and_18 (and_18_out, not_45_out, S1, not_46_out, I1, not_47_out);
  and and_19 (and_19_out, S2, S1, not_48_out, not_49_out);
  and and_20 (and_20_out, S2, S1, not_50_out, I0);
  and and_21 (and_21_out, S2, S1, not_51_out, I0);
  and and_22 (and_22_out, S2, S1, S0, I1, not_52_out);
  and and_23 (and_23_out, S3, S0);
  and and_24 (and_24_out, S3, S1);
  and and_25 (and_25_out, S3, S2);
  and and_26 (and_26_out, not_53_out, not_54_out, not_55_out, not_56_out);
  and and_27 (and_27_out, not_57_out, not_58_out, not_59_out, I0);
  and and_28 (and_28_out, not_60_out, not_61_out, I1, not_62_out);
  and and_29 (and_29_out, not_63_out, not_64_out, S0, not_65_out, not_66_out);
  and and_30 (and_30_out, not_67_out, S1, not_68_out, not_69_out, I0);
  and and_31 (and_31_out, not_70_out, S1, I1, not_71_out);
  and and_32 (and_32_out, not_72_out, S2, not_73_out, S0);
  and and_33 (and_33_out, not_74_out, S2, S0, I0);
  and and_34 (and_34_out, not_75_out, S2, S0, I1);
  and and_35 (and_35_out, S2, S1, not_76_out, not_77_out, not_78_out);
  and and_36 (and_36_out, S3, S2, S1, not_79_out);
  or or_1 (S31, and_1_out, and_2_out, and_3_out, and_4_out);
  or or_2 (S11, and_15_out, and_16_out, and_17_out, and_18_out, and_19_out, and_20_out, and_21_out, and_22_out, and_23_out, and_24_out, and_25_out);
  or or_3 (S01, and_26_out, and_27_out, and_28_out, and_29_out, and_30_out, and_31_out, and_32_out, and_33_out, and_34_out, and_35_out, and_36_out);
  or or_4 (S21, and_5_out, and_6_out, and_7_out, and_8_out, and_9_out, and_10_out, and_11_out, and_12_out, and_13_out, and_14_out);
endmodule

module \output  (
  input  S31,
  input  S21,
  input  S11,
  input  S01,
  output arr,
  output hit
);

  wire and_2_out, and_3_out, not_1_out, not_2_out;

  not not_1 (not_1_out, S11);
  and and_1 (arr, S21, not_1_out, not_2_out);
  not not_2 (not_2_out, S01);
  and and_2 (and_2_out, S21, S01);
  and and_3 (and_3_out, S21, S11);
  or or_1 (hit, and_2_out, and_3_out, S31);
endmodule
