// Logisim project p0_afterclass_ftoi.circ as structural Verilog: 2 circuits, main circuit ftoi
module ftoi (
  input  [15:0] float,
  output [31:0] \int 
);

  dataProcessing dataprocessing_1 (.float(float), .\int (\int ));
endmodule

module dataProcessing (
  input  [15:0] float,
  output [31:0] \int 
);

  wire comparator_1_lt, comparator_2_eq, comparator_3_eq, comparator_4_gt, or_2_out;
  wire [4:0] n, subtractor_1_out, subtractor_2_out;
  wire [31:0] adder_1_out, bit_extender_1_out, bit_extender_2_out, bit_extender_3_out, multiplexer_1_out,
       multiplexer_2_out, multiplexer_3_out, multiplexer_5_out, not_1_out, out, shifter_1_out, shifter_2_out,
       shifter_3_out, temp;

  Comparator #(.width(5), .mode("unsigned")) comparator_1 (.a(5'b01010), .b(n), .lt(comparator_1_lt));  // open: gt, eq
  assign bit_extender_1_out = {{22{1'b0}}, float[9:0]};  // Bit_Extender bit_extender_1
  Subtractor #(.width(5)) subtractor_1 (.a(5'b01010), .b(n), .out(subtractor_1_out));  // open: bin, bout
  assign bit_extender_2_out = {{22{1'b0}}, float[9:0]};  // Bit_Extender bit_extender_2
  Subtractor #(.width(5)) subtractor_2 (.a(n), .b(5'b01010), .out(subtractor_2_out));  // open: bin, bout
  Shifter #(.width(32), .shift("lr")) shifter_1 (
    .in(bit_extender_1_out), .\dist (subtractor_1_out), .out(shifter_1_out));
  Shifter #(.width(32)) shifter_2 (.in(bit_extender_2_out), .\dist (subtractor_2_out), .out(shifter_2_out));
  Multiplexer #(.width(32), .enable("false")) multiplexer_1 (
    .in0(temp), .in1({32{1'b0}}), .out(multiplexer_1_out), .sel(comparator_4_gt));
  Multiplexer #(.width(32), .enable("false")) multiplexer_2 (
    .in0(shifter_1_out), .in1(shifter_2_out), .out(multiplexer_2_out), .sel(comparator_1_lt));
  Multiplexer #(.width(32), .enable("false")) multiplexer_3 (
    .in0(multiplexer_1_out), .in1({32{1'b0}}), .out(multiplexer_3_out), .sel(comparator_2_eq));
  Comparator #(.width(5), .mode("unsigned")) comparator_2 (
    .a(float[14:10]), .b({5{1'b0}}), .eq(comparator_2_eq));  // open: gt, lt
  Comparator #(.width(5), .mode("unsigned")) comparator_3 (
    .a(float[14:10]), .b({5{1'b1}}), .eq(comparator_3_eq));  // open: gt, lt
  assign bit_extender_3_out = {{31{1'b0}}, 1'b1};  // Bit_Extender bit_extender_3
  Subtractor #(.width(5)) subtractor_3 (.a(float[14:10]), .b(5'b01111), .out(n));  // open: bin, bout
  Multiplexer #(.width(32), .enable("false")) multiplexer_4 (
    .in0(multiplexer_3_out), .in1({32{1'b0}}), .out(out), .sel(comparator_3_eq));
  Shifter #(.width(32)) shifter_3 (.in(bit_extender_3_out), .\dist (n), .out(shifter_3_out));
  Comparator #(.width(5)) comparator_4 (.a({5{1'b0}}), .b(n), .gt(comparator_4_gt));  // open: eq, lt
  // Probe on temp
  assign temp = multiplexer_2_out | shifter_3_out;  // OR_Gate or_1, 32 bits wide
  // Probe on multiplexer_5_out
  Multiplexer #(.width(32), .enable("false")) multiplexer_5 (
    .in0(out), .in1({32{1'b0}}), .out(multiplexer_5_out), .sel(or_2_out));
  or or_2 (or_2_out, comparator_2_eq, comparator_4_gt, comparator_3_eq);
  assign not_1_out = ~multiplexer_5_out;  // NOT_Gate not_1, 32 bits wide
  Adder #(.width(32)) adder_1 (.a(not_1_out), .b(32'h1), .out(adder_1_out));  // open: cin, cout
  Multiplexer #(.width(32), .enable("false")) multiplexer_6 (
    .in0(multiplexer_5_out), .in1(adder_1_out), .out(\int ), .sel(float[15]));

  // Other names for the same wires on the sheet: fraction[9:0] = float[9:0]; sign = float[15]

  // Notes on the sheet:
  //   if >, nagetive
endmodule
